// Digital circuit Controller.dig as structural Verilog
module Controller (
  input  Clk,
  input  Clr,
  input  I0,
  input  I1,
  input  I2,
  input  I3
);

  wire ring_counter_1_q0, ring_counter_1_q1, ring_counter_1_q2, ring_counter_1_q3, ring_counter_1_q4,
       selector_1_s0, selector_1_s1, selector_1_s2, selector_1_s3, selector_1_s4, selector_1_s5,
       selector_1_s6, selector_1_s7, selector_1_s8;

  Ring_Counter ring_counter_1 (
    .Clk(Clk), .Clr(Clr), .Q0(ring_counter_1_q0), .Q1(ring_counter_1_q1), .Q2(ring_counter_1_q2),
    .Q3(ring_counter_1_q3), .Q4(ring_counter_1_q4));
  Selector selector_1 (
    .A(I0), .B(I1), .C(I2), .D(I3), .S0(selector_1_s0), .S1(selector_1_s1), .S2(selector_1_s2),
    .S3(selector_1_s3), .S4(selector_1_s4), .S5(selector_1_s5), .S6(selector_1_s6), .S7(selector_1_s7),
    .S8(selector_1_s8));

  // Notes on the sheet:
  //   EXECUTE:
  //   Cp Ep NLm NCE Ad  NLi NEi NLa Ea  Eu NLb NLa
  //   0    1     0     1    1     1   1     1    0   0    1     1
  //   FETCH:
  //   T2:
  //   Cp Ep NLm NCE Ad  NLi NEi NLa Ea  Eu NLb NLa
  //   1    0     1     1    1     1   1     1    0   0    1     1
  //   T1:
  //   Cp Ep NLm NCE Ad  NLi NEi NLa Ea  Eu NLb NLa
  //   1    0     1     1    1     1   1     1    0   0    1     1
  //   T0:
  //   Cp Ep NLm NCE Ad  NLi NEi NLa Ea  Eu NLb NLa
  //   0    1     0     1    1     1   1     1    0   0    1     1
endmodule
